// Logisim project CPU.circ as structural Verilog: 24 circuits, main circuit Examples
module Examples (
  input  [7:0] in_1,
  input  [7:0] in_2,
  input  [7:0] in_3,
  input  [7:0] in_4,
  input  [7:0] in_5
);

  wire blockbottom_1_out_5, blockbottom_1_out_6, blockbottom_1_out_7, blockbottom_1_out_8,
       blockbottom_1_out_9, blockbottom_1_out_10, blockbottom_1_out_11, blockbottom_1_out_12,
       blockbottom_1_out_13, blockbottom_1_out_14, blockbottom_1_out_15, blockbottom_1_out_16,
       blockbottom_1_out_17, blockbottom_1_out_18, blockbottom_1_out_19, blockbottom_1_out_20,
       blocktop_1_out_5, blocktop_1_out_6, blocktop_1_out_7, blocktop_1_out_8, blocktop_1_out_9,
       blocktop_1_out_10, blocktop_1_out_11, blocktop_1_out_12, blocktop_1_out_13, blocktop_1_out_14,
       blocktop_1_out_15, blocktop_1_out_16, blocktop_1_out_17, blocktop_1_out_18, blocktop_1_out_19,
       blocktop_1_out_20, converterbottom_1_out_2, converterbottom_1_out_3, converterbottom_1_out_4,
       converterbottom_1_out_5, convertertop_1_out_2, convertertop_1_out_3, convertertop_1_out_4,
       convertertop_1_out_5;
  wire [7:0] blackbox_1_out_5, blackbox_1_out_6, blackbox_1_out_7, blackbox_1_out_8;

  ConverterTop convertertop_1 (
    .in_1(in_1), .out_2(convertertop_1_out_2), .out_3(convertertop_1_out_3), .out_4(convertertop_1_out_4),
    .out_5(convertertop_1_out_5));
  _7_Segment_Display #(.active("true")) u_7_segment_display_1 (
    .g(convertertop_1_out_2), .f(convertertop_1_out_3), .a(convertertop_1_out_4), .b(convertertop_1_out_5),
    .e(converterbottom_1_out_2), .d(converterbottom_1_out_3), .c(converterbottom_1_out_4),
    .dp(converterbottom_1_out_5));
  ConverterBottom converterbottom_1 (
    .in_1(in_1), .out_2(converterbottom_1_out_2), .out_3(converterbottom_1_out_3),
    .out_4(converterbottom_1_out_4), .out_5(converterbottom_1_out_5));
  _7_Segment_Display #(.active("true")) u_7_segment_display_2 (
    .g(blocktop_1_out_5), .f(blocktop_1_out_13), .a(blocktop_1_out_14), .b(blocktop_1_out_6),
    .e(blockbottom_1_out_13), .d(blockbottom_1_out_5), .c(blockbottom_1_out_6), .dp(blockbottom_1_out_14));
  BlockBottom blockbottom_1 (
    .out_13(blockbottom_1_out_13), .out_5(blockbottom_1_out_5), .out_6(blockbottom_1_out_6),
    .out_14(blockbottom_1_out_14), .out_15(blockbottom_1_out_15), .out_7(blockbottom_1_out_7),
    .out_8(blockbottom_1_out_8), .out_16(blockbottom_1_out_16), .out_17(blockbottom_1_out_17),
    .out_9(blockbottom_1_out_9), .out_10(blockbottom_1_out_10), .out_18(blockbottom_1_out_18),
    .out_19(blockbottom_1_out_19), .out_11(blockbottom_1_out_11), .out_12(blockbottom_1_out_12),
    .out_20(blockbottom_1_out_20), .in_1(blackbox_1_out_5), .in_2(blackbox_1_out_6), .in_3(blackbox_1_out_7),
    .in_4(blackbox_1_out_8));
  BlockTop blocktop_1 (
    .in_1(blackbox_1_out_5), .in_2(blackbox_1_out_6), .in_3(blackbox_1_out_7), .in_4(blackbox_1_out_8),
    .out_5(blocktop_1_out_5), .out_13(blocktop_1_out_13), .out_14(blocktop_1_out_14),
    .out_6(blocktop_1_out_6), .out_7(blocktop_1_out_7), .out_15(blocktop_1_out_15),
    .out_16(blocktop_1_out_16), .out_8(blocktop_1_out_8), .out_9(blocktop_1_out_9),
    .out_17(blocktop_1_out_17), .out_18(blocktop_1_out_18), .out_10(blocktop_1_out_10),
    .out_11(blocktop_1_out_11), .out_19(blocktop_1_out_19), .out_20(blocktop_1_out_20),
    .out_12(blocktop_1_out_12));
  _7_Segment_Display #(.active("true")) u_7_segment_display_3 (
    .g(blocktop_1_out_9), .f(blocktop_1_out_17), .a(blocktop_1_out_18), .b(blocktop_1_out_10),
    .e(blockbottom_1_out_17), .d(blockbottom_1_out_9), .c(blockbottom_1_out_10), .dp(blockbottom_1_out_18));
  _7_Segment_Display #(.active("true")) u_7_segment_display_4 (
    .g(blocktop_1_out_7), .f(blocktop_1_out_15), .a(blocktop_1_out_16), .b(blocktop_1_out_8),
    .e(blockbottom_1_out_15), .d(blockbottom_1_out_7), .c(blockbottom_1_out_8), .dp(blockbottom_1_out_16));
  blackbox blackbox_1 (
    .out_5(blackbox_1_out_5), .out_6(blackbox_1_out_6), .out_7(blackbox_1_out_7), .out_8(blackbox_1_out_8),
    .in_1(in_2), .in_2(in_3), .in_3(in_4), .in_4(in_5));
  _7_Segment_Display #(.active("true")) u_7_segment_display_5 (
    .g(blocktop_1_out_11), .f(blocktop_1_out_19), .a(blocktop_1_out_20), .b(blocktop_1_out_12),
    .e(blockbottom_1_out_19), .d(blockbottom_1_out_11), .c(blockbottom_1_out_12), .dp(blockbottom_1_out_20));

  // Notes on the sheet:
  //   ConverterTop
  //   ConverterBottom
  //   Displayed Value
  //   Seven Segment Display
  //   DISP[3]
  //   DISP[1]
  //   DISP[2]
  //   DISP[2]
  //   DISP[0]
  //   Your Display Logic
  //   BlockTop
  //   BlockBottom
endmodule

module Converter (
  input  [7:0] in_1,
  output out_2,
  output out_3,
  output out_4,
  output out_5,
  output out_6,
  output out_7,
  output out_8,
  output out_9
);

  wire and_1_out, or_1_out;
  wire [7:0] multiplexer_1_out, multiplexer_2_out;

  Multiplexer #(.select(4), .width(8), .disabled("Z"), .enable("false")) multiplexer_1 (
    .in0(8'h77), .in1(8'h41), .in2(8'h3b), .in3(8'h6b), .in4(8'h4d), .in5(8'h6e), .in6(8'h7e), .in7(8'h43),
    .in8(8'h7f), .in9(8'h6f), .in10(8'h5f), .in11(8'h7c), .in12(8'h36), .in13(8'h79), .in14(8'h3e),
    .in15(8'h1e), .out(multiplexer_1_out), .sel(in_1[3:0]));
  or or_1 (or_1_out, in_1[4], in_1[5], in_1[6], in_1[7]);
  Multiplexer #(.select(1), .width(8), .disabled("Z"), .enable("false")) multiplexer_2 (
    .in0(multiplexer_1_out), .in1(8'h9b), .out(multiplexer_2_out), .sel(or_1_out));
  and and_1 (and_1_out, in_1[0], in_1[1], in_1[2], in_1[3], in_1[4], in_1[5], in_1[6], in_1[7]);
  Multiplexer #(.select(1), .width(8), .disabled("Z"), .enable("false")) multiplexer_3 (
    .in0(multiplexer_2_out), .in1({8{1'b0}}), .out({out_9, out_8, out_7, out_6, out_2, out_3, out_4, out_5}),
    .sel(and_1_out));

  // Notes on the sheet:
  //   0
  //   1
  //   2
  //   3
  //   4
  //   5
  //   6
  //   7
  //   8
  //   9
  //   a
  //   b
  //   c
  //   d
  //   e
  //   f
  //   ?
endmodule

module ConverterTop (
  input  [7:0] in_1,
  output out_2,
  output out_3,
  output out_4,
  output out_5
);

  wire and_1_out, or_1_out;
  wire [7:0] multiplexer_1_out, multiplexer_2_out;
  wire [7:4] multiplexer_3_out;

  Multiplexer #(.select(4), .width(8), .disabled("Z"), .enable("false")) multiplexer_1 (
    .in0(8'h77), .in1(8'h41), .in2(8'h3b), .in3(8'h6b), .in4(8'h4d), .in5(8'h6e), .in6(8'h7e), .in7(8'h43),
    .in8(8'h7f), .in9(8'h6f), .in10(8'h5f), .in11(8'h7c), .in12(8'h36), .in13(8'h79), .in14(8'h3e),
    .in15(8'h1e), .out(multiplexer_1_out), .sel(in_1[3:0]));
  or or_1 (or_1_out, in_1[4], in_1[5], in_1[6], in_1[7]);
  Multiplexer #(.select(1), .width(8), .disabled("Z"), .enable("false")) multiplexer_2 (
    .in0(multiplexer_1_out), .in1(8'h9b), .out(multiplexer_2_out), .sel(or_1_out));
  and and_1 (and_1_out, in_1[0], in_1[1], in_1[2], in_1[3], in_1[4], in_1[5], in_1[6], in_1[7]);
  Multiplexer #(.select(1), .width(8), .disabled("Z"), .enable("false")) multiplexer_3 (
    .in0(multiplexer_2_out), .in1({8{1'b0}}), .out({multiplexer_3_out, out_2, out_3, out_4, out_5}),
    .sel(and_1_out));

  // Notes on the sheet:
  //   0
  //   1
  //   2
  //   3
  //   4
  //   5
  //   6
  //   7
  //   8
  //   9
  //   a
  //   b
  //   c
  //   d
  //   e
  //   f
  //   ?
endmodule

module ConverterBottom (
  input  [7:0] in_1,
  output out_2,
  output out_3,
  output out_4,
  output out_5
);

  wire and_1_out, or_1_out;
  wire [3:0] multiplexer_3_out;
  wire [7:0] multiplexer_1_out, multiplexer_2_out;

  Multiplexer #(.select(4), .width(8), .disabled("Z"), .enable("false")) multiplexer_1 (
    .in0(8'h77), .in1(8'h41), .in2(8'h3b), .in3(8'h6b), .in4(8'h4d), .in5(8'h6e), .in6(8'h7e), .in7(8'h43),
    .in8(8'h7f), .in9(8'h6f), .in10(8'h5f), .in11(8'h7c), .in12(8'h36), .in13(8'h79), .in14(8'h3e),
    .in15(8'h1e), .out(multiplexer_1_out), .sel(in_1[3:0]));
  or or_1 (or_1_out, in_1[4], in_1[5], in_1[6], in_1[7]);
  Multiplexer #(.select(1), .width(8), .disabled("Z"), .enable("false")) multiplexer_2 (
    .in0(multiplexer_1_out), .in1(8'h9b), .out(multiplexer_2_out), .sel(or_1_out));
  and and_1 (and_1_out, in_1[0], in_1[1], in_1[2], in_1[3], in_1[4], in_1[5], in_1[6], in_1[7]);
  Multiplexer #(.select(1), .width(8), .disabled("Z"), .enable("false")) multiplexer_3 (
    .in0(multiplexer_2_out), .in1({8{1'b0}}), .out({out_5, out_4, out_3, out_2, multiplexer_3_out}),
    .sel(and_1_out));

  // Notes on the sheet:
  //   0
  //   1
  //   2
  //   3
  //   4
  //   5
  //   6
  //   7
  //   8
  //   9
  //   a
  //   b
  //   c
  //   d
  //   e
  //   f
  //   ?
endmodule

module blackbox (
  input  [7:0] in_1,
  input  [7:0] in_2,
  input  [7:0] in_3,
  input  [7:0] in_4,
  output [7:0] out_5,
  output [7:0] out_6,
  output [7:0] out_7,
  output [7:0] out_8
);


  assign out_5 = in_1;
  assign out_6 = in_2;
  assign out_7 = in_3;
  assign out_8 = in_4;
endmodule

module BlockTop (
  input  [7:0] in_1,
  input  [7:0] in_2,
  input  [7:0] in_3,
  input  [7:0] in_4,
  output out_5,
  output out_6,
  output out_7,
  output out_8,
  output out_9,
  output out_10,
  output out_11,
  output out_12,
  output out_13,
  output out_14,
  output out_15,
  output out_16,
  output out_17,
  output out_18,
  output out_19,
  output out_20
);

  ConverterTop convertertop_1 (.in_1(in_1), .out_2(out_5), .out_3(out_13), .out_4(out_14), .out_5(out_6));
  ConverterTop convertertop_2 (.in_1(in_2), .out_2(out_7), .out_3(out_15), .out_4(out_16), .out_5(out_8));
  ConverterTop convertertop_3 (.in_1(in_3), .out_2(out_9), .out_3(out_17), .out_4(out_18), .out_5(out_10));
  ConverterTop convertertop_4 (.in_1(in_4), .out_2(out_11), .out_3(out_19), .out_4(out_20), .out_5(out_12));
endmodule

module \寄存器堆  (
  input  [1:0] rd_rt,
  input  [1:0] rs,
  input  [15:0] in_3,
  input  [1:0] rt,
  input  cl,
  input  write_enable,
  output [15:0] out_7,
  output [15:0] out_8
);

  wire and_1_out, and_2_out, and_3_out, and_4_out, demultiplexer_1_out0, demultiplexer_1_out1,
       demultiplexer_1_out2, demultiplexer_1_out3;
  wire [15:0] register_1_q, register_2_q, register_3_q, register_4_q;

  Demultiplexer #(.select(2), .width(1), .tristate("false"), .disabled("Z"), .enable("false")) demultiplexer_1 (
    .out0(demultiplexer_1_out0), .out1(demultiplexer_1_out1), .out2(demultiplexer_1_out2),
    .out3(demultiplexer_1_out3), .in(1'b1), .sel(rd_rt));
  and and_1 (and_1_out, demultiplexer_1_out0, cl, write_enable);
  and and_2 (and_2_out, demultiplexer_1_out1, cl, write_enable);
  and and_3 (and_3_out, demultiplexer_1_out2, cl, write_enable);
  and and_4 (and_4_out, demultiplexer_1_out3, cl, write_enable);
  Register #(.width(16), .trigger("rising"), .Select("low")) register_1 (
    .D(in_3), .en(and_1_out), .Q(register_1_q), .clk(and_1_out));  // open: clr
  Register #(.width(16), .trigger("rising"), .Select("low")) register_2 (
    .D(in_3), .en(and_2_out), .Q(register_2_q), .clk(and_2_out));  // open: clr
  Register #(.width(16), .trigger("rising"), .Select("low")) register_3 (
    .D(in_3), .en(and_3_out), .Q(register_3_q), .clk(and_3_out));  // open: clr
  Register #(.width(16), .trigger("rising"), .Select("low")) register_4 (
    .D(in_3), .en(and_4_out), .Q(register_4_q), .clk(and_4_out));  // open: clr
  Multiplexer #(.select(2), .width(16), .disabled("Z"), .enable("false")) multiplexer_1 (
    .in0(register_1_q), .in1(register_2_q), .in2(register_3_q), .in3(register_4_q), .out(out_7), .sel(rs));
  Multiplexer #(.select(2), .width(16), .disabled("Z"), .enable("false")) multiplexer_2 (
    .in0(register_1_q), .in1(register_2_q), .in2(register_3_q), .in3(register_4_q), .out(out_8), .sel(rt));

  // Notes on the sheet:
  //   0（00）
  //   1（01）
  //   2（10）
  //   3（11）
endmodule

module BlockBottom (
  input  [7:0] in_1,
  input  [7:0] in_2,
  input  [7:0] in_3,
  input  [7:0] in_4,
  output out_5,
  output out_6,
  output out_7,
  output out_8,
  output out_9,
  output out_10,
  output out_11,
  output out_12,
  output out_13,
  output out_14,
  output out_15,
  output out_16,
  output out_17,
  output out_18,
  output out_19,
  output out_20
);

  ConverterBottom converterbottom_1 (.in_1(in_1), .out_2(out_13), .out_3(out_5), .out_4(out_6), .out_5(out_14));
  ConverterBottom converterbottom_2 (.in_1(in_2), .out_2(out_15), .out_3(out_7), .out_4(out_8), .out_5(out_16));
  ConverterBottom converterbottom_3 (.in_1(in_3), .out_2(out_17), .out_3(out_9), .out_4(out_10), .out_5(out_18));
  ConverterBottom converterbottom_4 (.in_1(in_4), .out_2(out_19), .out_3(out_11), .out_4(out_12), .out_5(out_20));
endmodule

module ALU (
  input  [1:0] in_1,
  input  [15:0] A,
  input  [15:0] B,
  output [15:0] out_4
);

  wire [15:0] and_out_48, or_out_48, \减法_out_50 , \加法_out_50 ;

  Multiplexer #(.select(2), .width(16), .disabled("Z"), .enable("false")) multiplexer_1 (
    .in0(or_out_48), .in1(and_out_48), .in2(\加法_out_50 ), .in3(\减法_out_50 ), .out(out_4), .sel(in_1));
  or_ALU \or  (
    .out_33(or_out_48[15]), .out_34(or_out_48[14]), .out_35(or_out_48[13]), .out_36(or_out_48[12]),
    .out_37(or_out_48[11]), .out_38(or_out_48[10]), .out_39(or_out_48[9]), .out_40(or_out_48[8]),
    .out_41(or_out_48[7]), .out_42(or_out_48[6]), .out_43(or_out_48[5]), .out_44(or_out_48[4]),
    .out_45(or_out_48[3]), .out_46(or_out_48[2]), .out_47(or_out_48[1]), .out_48(or_out_48[0]), .in_1(A[15]),
    .in_17(B[15]), .in_2(A[14]), .in_18(B[14]), .in_3(A[13]), .in_19(B[13]), .in_4(A[12]), .in_20(B[12]),
    .in_5(A[11]), .in_21(B[11]), .in_6(A[10]), .in_22(B[10]), .in_7(A[9]), .in_23(B[9]), .in_8(A[8]),
    .in_24(B[8]), .in_9(A[7]), .in_25(B[7]), .in_10(A[6]), .in_26(B[6]), .in_11(A[5]), .in_27(B[5]),
    .in_12(A[4]), .in_28(B[4]), .in_13(A[3]), .in_29(B[3]), .in_14(A[2]), .in_30(B[2]), .in_15(A[1]),
    .in_31(B[1]), .in_16(A[0]), .in_32(B[0]));
  and_ALU \and  (
    .out_33(and_out_48[15]), .out_34(and_out_48[14]), .out_35(and_out_48[13]), .out_36(and_out_48[12]),
    .out_37(and_out_48[11]), .out_38(and_out_48[10]), .out_39(and_out_48[9]), .out_40(and_out_48[8]),
    .out_41(and_out_48[7]), .out_42(and_out_48[6]), .out_43(and_out_48[5]), .out_44(and_out_48[4]),
    .out_45(and_out_48[3]), .out_46(and_out_48[2]), .out_47(and_out_48[1]), .out_48(and_out_48[0]),
    .in_1(A[15]), .in_17(B[15]), .in_2(A[14]), .in_18(B[14]), .in_3(A[13]), .in_19(B[13]), .in_4(A[12]),
    .in_20(B[12]), .in_5(A[11]), .in_21(B[11]), .in_6(A[10]), .in_22(B[10]), .in_7(A[9]), .in_23(B[9]),
    .in_8(A[8]), .in_24(B[8]), .in_9(A[7]), .in_25(B[7]), .in_10(A[6]), .in_26(B[6]), .in_11(A[5]),
    .in_27(B[5]), .in_12(A[4]), .in_28(B[4]), .in_13(A[3]), .in_29(B[3]), .in_14(A[2]), .in_30(B[2]),
    .in_15(A[1]), .in_31(B[1]), .in_16(A[0]), .in_32(B[0]));
  \_16加法器  \u_减法  (
    .in_1(1'b1), .out_35(\减法_out_50 [15]), .out_36(\减法_out_50 [14]), .out_37(\减法_out_50 [13]),
    .out_38(\减法_out_50 [12]), .out_39(\减法_out_50 [11]), .out_40(\减法_out_50 [10]), .out_41(\减法_out_50 [9]),
    .out_42(\减法_out_50 [8]), .out_43(\减法_out_50 [7]), .out_44(\减法_out_50 [6]), .out_45(\减法_out_50 [5]),
    .out_46(\减法_out_50 [4]), .out_47(\减法_out_50 [3]), .out_48(\减法_out_50 [2]), .out_49(\减法_out_50 [1]),
    .out_50(\减法_out_50 [0]), .in_2(A[15]), .in_18(B[15]), .in_3(A[14]), .in_19(B[14]), .in_4(A[13]),
    .in_20(B[13]), .in_5(A[12]), .in_21(B[12]), .in_6(A[11]), .in_22(B[11]), .in_7(A[10]), .in_23(B[10]),
    .in_8(A[9]), .in_24(B[9]), .in_9(A[8]), .in_25(B[8]), .in_10(A[7]), .in_26(B[7]), .in_11(A[6]),
    .in_27(B[6]), .in_12(A[5]), .in_28(B[5]), .in_13(A[4]), .in_29(B[4]), .in_14(A[3]), .in_30(B[3]),
    .in_15(A[2]), .in_31(B[2]), .in_16(A[1]), .in_32(B[1]), .in_17(A[0]), .in_33(B[0]));  // open: out_51, out_34
  \_16加法器  \u_加法  (
    .in_1(1'b0), .out_35(\加法_out_50 [15]), .out_36(\加法_out_50 [14]), .out_37(\加法_out_50 [13]),
    .out_38(\加法_out_50 [12]), .out_39(\加法_out_50 [11]), .out_40(\加法_out_50 [10]), .out_41(\加法_out_50 [9]),
    .out_42(\加法_out_50 [8]), .out_43(\加法_out_50 [7]), .out_44(\加法_out_50 [6]), .out_45(\加法_out_50 [5]),
    .out_46(\加法_out_50 [4]), .out_47(\加法_out_50 [3]), .out_48(\加法_out_50 [2]), .out_49(\加法_out_50 [1]),
    .out_50(\加法_out_50 [0]), .in_2(A[15]), .in_18(B[15]), .in_3(A[14]), .in_19(B[14]), .in_4(A[13]),
    .in_20(B[13]), .in_5(A[12]), .in_21(B[12]), .in_6(A[11]), .in_22(B[11]), .in_7(A[10]), .in_23(B[10]),
    .in_8(A[9]), .in_24(B[9]), .in_9(A[8]), .in_25(B[8]), .in_10(A[7]), .in_26(B[7]), .in_11(A[6]),
    .in_27(B[6]), .in_12(A[5]), .in_28(B[5]), .in_13(A[4]), .in_29(B[4]), .in_14(A[3]), .in_30(B[3]),
    .in_15(A[2]), .in_31(B[2]), .in_16(A[1]), .in_32(B[1]), .in_17(A[0]), .in_33(B[0]));  // open: out_51, out_34

  // Notes on the sheet:
  //   00是or
  //   01是and
  //   10是加法
  //   11是减法（A-B）
endmodule

module \_16加法器  (
  input  in_1,
  input  in_2,
  input  in_3,
  input  in_4,
  input  in_5,
  input  in_6,
  input  in_7,
  input  in_8,
  input  in_9,
  input  in_10,
  input  in_11,
  input  in_12,
  input  in_13,
  input  in_14,
  input  in_15,
  input  in_16,
  input  in_17,
  input  in_18,
  input  in_19,
  input  in_20,
  input  in_21,
  input  in_22,
  input  in_23,
  input  in_24,
  input  in_25,
  input  in_26,
  input  in_27,
  input  in_28,
  input  in_29,
  input  in_30,
  input  in_31,
  input  in_32,
  input  in_33,
  output out_34,
  output out_35,
  output out_36,
  output out_37,
  output out_38,
  output out_39,
  output out_40,
  output out_41,
  output out_42,
  output out_43,
  output out_44,
  output out_45,
  output out_46,
  output out_47,
  output out_48,
  output out_49,
  output out_50,
  output out_51
);

  wire fa_2_out_4, fa_3_out_4, fa_4_out_4, fa_5_out_4, fa_6_out_4, fa_7_out_4, fa_8_out_4, fa_9_out_4,
       fa_10_out_4, fa_11_out_4, fa_12_out_4, fa_13_out_4, fa_14_out_4, fa_15_out_4, fa_16_out_4, xor_2_out,
       xor_3_out, xor_4_out, xor_5_out, xor_6_out, xor_7_out, xor_8_out, xor_9_out, xor_10_out, xor_11_out,
       xor_12_out, xor_13_out, xor_14_out, xor_15_out, xor_16_out, xor_17_out;

  xor xor_1 (out_34, out_51, fa_2_out_4);
  FA fa_1 (.out_4(out_51), .out_5(out_35), .in_1(fa_2_out_4), .in_2(in_2), .in_3(xor_2_out));
  FA fa_2 (.out_4(fa_2_out_4), .out_5(out_36), .in_1(fa_3_out_4), .in_2(in_3), .in_3(xor_4_out));
  xor xor_2 (xor_2_out, in_1, in_18);
  FA fa_3 (.out_4(fa_3_out_4), .out_5(out_37), .in_1(fa_4_out_4), .in_2(in_4), .in_3(xor_3_out));
  xor xor_3 (xor_3_out, in_1, in_20);
  xor xor_4 (xor_4_out, in_1, in_19);
  FA fa_4 (.out_4(fa_4_out_4), .out_5(out_38), .in_1(fa_5_out_4), .in_2(in_5), .in_3(xor_5_out));
  xor xor_5 (xor_5_out, in_1, in_21);
  FA fa_5 (.out_4(fa_5_out_4), .out_5(out_39), .in_1(fa_6_out_4), .in_2(in_6), .in_3(xor_6_out));
  xor xor_6 (xor_6_out, in_1, in_22);
  FA fa_6 (.out_4(fa_6_out_4), .out_5(out_40), .in_1(fa_7_out_4), .in_2(in_7), .in_3(xor_7_out));
  FA fa_7 (.out_4(fa_7_out_4), .out_5(out_41), .in_1(fa_8_out_4), .in_2(in_8), .in_3(xor_9_out));
  xor xor_7 (xor_7_out, in_1, in_23);
  FA fa_8 (.out_4(fa_8_out_4), .out_5(out_42), .in_1(fa_9_out_4), .in_2(in_9), .in_3(xor_8_out));
  xor xor_8 (xor_8_out, in_1, in_25);
  xor xor_9 (xor_9_out, in_1, in_24);
  FA fa_9 (.out_4(fa_9_out_4), .out_5(out_43), .in_1(fa_10_out_4), .in_2(in_10), .in_3(xor_10_out));
  xor xor_10 (xor_10_out, in_1, in_26);
  FA fa_10 (.out_4(fa_10_out_4), .out_5(out_44), .in_1(fa_11_out_4), .in_2(in_11), .in_3(xor_11_out));
  xor xor_11 (xor_11_out, in_1, in_27);
  FA fa_11 (.out_4(fa_11_out_4), .out_5(out_45), .in_1(fa_12_out_4), .in_2(in_12), .in_3(xor_12_out));
  xor xor_12 (xor_12_out, in_1, in_28);
  FA fa_12 (.out_4(fa_12_out_4), .out_5(out_46), .in_1(fa_13_out_4), .in_2(in_13), .in_3(xor_13_out));
  FA fa_13 (.out_4(fa_13_out_4), .out_5(out_47), .in_1(fa_14_out_4), .in_2(in_14), .in_3(xor_14_out));
  xor xor_13 (xor_13_out, in_1, in_29);
  FA fa_14 (.out_4(fa_14_out_4), .out_5(out_48), .in_1(fa_15_out_4), .in_2(in_15), .in_3(xor_15_out));
  xor xor_14 (xor_14_out, in_1, in_30);
  xor xor_15 (xor_15_out, in_1, in_31);
  FA fa_15 (.out_4(fa_15_out_4), .out_5(out_49), .in_1(fa_16_out_4), .in_2(in_16), .in_3(xor_16_out));
  xor xor_16 (xor_16_out, in_1, in_32);
  FA fa_16 (.out_4(fa_16_out_4), .out_5(out_50), .in_1(in_1), .in_2(in_17), .in_3(xor_17_out));
  xor xor_17 (xor_17_out, in_1, in_33);
endmodule

module or_ALU (
  input  in_1,
  input  in_2,
  input  in_3,
  input  in_4,
  input  in_5,
  input  in_6,
  input  in_7,
  input  in_8,
  input  in_9,
  input  in_10,
  input  in_11,
  input  in_12,
  input  in_13,
  input  in_14,
  input  in_15,
  input  in_16,
  input  in_17,
  input  in_18,
  input  in_19,
  input  in_20,
  input  in_21,
  input  in_22,
  input  in_23,
  input  in_24,
  input  in_25,
  input  in_26,
  input  in_27,
  input  in_28,
  input  in_29,
  input  in_30,
  input  in_31,
  input  in_32,
  output out_33,
  output out_34,
  output out_35,
  output out_36,
  output out_37,
  output out_38,
  output out_39,
  output out_40,
  output out_41,
  output out_42,
  output out_43,
  output out_44,
  output out_45,
  output out_46,
  output out_47,
  output out_48
);

  or or_1 (out_34, in_2, in_18);
  or or_2 (out_33, in_1, in_17);
  or or_3 (out_36, in_4, in_20);
  or or_4 (out_35, in_3, in_19);
  or or_5 (out_37, in_5, in_21);
  or or_6 (out_38, in_6, in_22);
  or or_7 (out_40, in_8, in_24);
  or or_8 (out_39, in_7, in_23);
  or or_9 (out_41, in_9, in_25);
  or or_10 (out_42, in_10, in_26);
  or or_11 (out_44, in_12, in_28);
  or or_12 (out_43, in_11, in_27);
  or or_13 (out_46, in_14, in_30);
  or or_14 (out_45, in_13, in_29);
  or or_15 (out_47, in_15, in_31);
  or or_16 (out_48, in_16, in_32);
endmodule

module and_ALU (
  input  in_1,
  input  in_2,
  input  in_3,
  input  in_4,
  input  in_5,
  input  in_6,
  input  in_7,
  input  in_8,
  input  in_9,
  input  in_10,
  input  in_11,
  input  in_12,
  input  in_13,
  input  in_14,
  input  in_15,
  input  in_16,
  input  in_17,
  input  in_18,
  input  in_19,
  input  in_20,
  input  in_21,
  input  in_22,
  input  in_23,
  input  in_24,
  input  in_25,
  input  in_26,
  input  in_27,
  input  in_28,
  input  in_29,
  input  in_30,
  input  in_31,
  input  in_32,
  output out_33,
  output out_34,
  output out_35,
  output out_36,
  output out_37,
  output out_38,
  output out_39,
  output out_40,
  output out_41,
  output out_42,
  output out_43,
  output out_44,
  output out_45,
  output out_46,
  output out_47,
  output out_48
);

  and and_1 (out_34, in_2, in_18);
  and and_2 (out_33, in_1, in_17);
  and and_3 (out_36, in_4, in_20);
  and and_4 (out_35, in_3, in_19);
  and and_5 (out_37, in_5, in_21);
  and and_6 (out_38, in_6, in_22);
  and and_7 (out_40, in_8, in_24);
  and and_8 (out_39, in_7, in_23);
  and and_9 (out_42, in_10, in_26);
  and and_10 (out_41, in_9, in_25);
  and and_11 (out_43, in_11, in_27);
  and and_12 (out_44, in_12, in_28);
  and and_13 (out_46, in_14, in_30);
  and and_14 (out_45, in_13, in_29);
  and and_15 (out_47, in_15, in_31);
  and and_16 (out_48, in_16, in_32);
endmodule

module \CPU_______主电路  (
  input  [7:0] in_1,
  input  [7:0] in_2,
  input  [3:0] in_3,
  input  [3:0] in_4
);

  wire ALU_out_5, and_1_out, blockbottom_1_out_5, blockbottom_1_out_6, blockbottom_1_out_7,
       blockbottom_1_out_8, blockbottom_1_out_9, blockbottom_1_out_10, blockbottom_1_out_11,
       blockbottom_1_out_12, blockbottom_1_out_13, blockbottom_1_out_14, blockbottom_1_out_15,
       blockbottom_1_out_16, blockbottom_1_out_17, blockbottom_1_out_18, blockbottom_1_out_19,
       blockbottom_1_out_20, blocktop_1_out_5, blocktop_1_out_6, blocktop_1_out_7, blocktop_1_out_8,
       blocktop_1_out_9, blocktop_1_out_10, blocktop_1_out_11, blocktop_1_out_12, blocktop_1_out_13,
       blocktop_1_out_14, blocktop_1_out_15, blocktop_1_out_16, blocktop_1_out_17, blocktop_1_out_18,
       blocktop_1_out_19, blocktop_1_out_20, \bne_beq信号处理_1_x , clock_1_out, not_1_out, \控制器_alusrc ,
       \控制器_branch , \控制器_display , \控制器_jump , \控制器_lui , \控制器_memtoreg , \控制器_memwrite , \控制器_regdst ,
       \控制器_regwrite , \控制器_unequal , \时钟状态选择_1_out_2 , \时钟状态选择_1_out_3 , \时钟状态选择_1_out_4 ;
  wire [1:0] multiplexer_3_out;
  wire [2:0] \控制器_out_13 ;
  wire [7:0] blackbox_1_out_5, blackbox_1_out_6, blackbox_1_out_7, blackbox_1_out_8, demultiplexer_1_out1,
       demultiplexer_2_out1;
  wire [11:0] shifter_1_out;
  wire [15:0] ALU_out_4, bit_extender_1_out, multiplexer_1_out, multiplexer_2_out, multiplexer_4_out,
       multiplexer_5_out, multiplexer_6_out, multiplexer_7_out, \n16位移位器_1_out_3 , \n16封装加法器_1_out_3 ,
       pc_1_out_3, ram_1_data, register_1_q, rom_1_data, \寄存器堆_out_7 , \寄存器堆_out_8 ;

  Multiplexer #(.select(1), .width(16), .disabled("Z"), .enable("false")) multiplexer_1 (
    .in0(pc_1_out_3), .in1(\n16封装加法器_1_out_3 ), .out(multiplexer_1_out), .sel(and_1_out));
  Clock #(.highDuration(1), .lowDuration(1)) clock_1 (.out(clock_1_out));
  Multiplexer #(.select(1), .width(16), .disabled("Z"), .enable("false")) multiplexer_2 (
    .in0(multiplexer_1_out), .in1({pc_1_out_3[15:12], shifter_1_out}), .out(multiplexer_2_out),
    .sel(\控制器_jump ));
  \时钟状态选择  \u_时钟状态选择_1  (
    .out_2(\时钟状态选择_1_out_2 ), .out_3(\时钟状态选择_1_out_3 ), .out_4(\时钟状态选择_1_out_4 ), .in_1(clock_1_out));
  Register #(.width(16), .trigger("rising"), .Select("low")) register_1 (
    .D(multiplexer_2_out), .Q(register_1_q), .clk(\时钟状态选择_1_out_2 ));  // open: en, clr
  Shifter #(.width(12), .shift("ll")) shifter_1 (.in(rom_1_data[11:0]), .\dist (in_4), .out(shifter_1_out));
  ROM #(.addrWidth(16), .dataWidth(16), .Select("low")) rom_1 (.addr(register_1_q), .data(rom_1_data));
  \_16封装加法器  pc_1 (.out_3(pc_1_out_3), .in_1(register_1_q), .in_2(16'h1));
  control_test2 \u_控制器  (
    .jump(\控制器_jump ), .MemToReg(\控制器_memtoreg ), .MemWrite(\控制器_memwrite ), .branch(\控制器_branch ),
    .AluSrc(\控制器_alusrc ), .RegWrite(\控制器_regwrite ), .display(\控制器_display ), .regDst(\控制器_regdst ),
    .lui(\控制器_lui ), .unequal(\控制器_unequal ), .in_1(rom_1_data[15:12]), .in_2(rom_1_data[2:0]),
    .out_13(\控制器_out_13 ));
  Multiplexer #(.select(1), .width(2), .disabled("Z"), .enable("false")) multiplexer_3 (
    .in0(rom_1_data[9:8]), .in1(rom_1_data[7:6]), .out(multiplexer_3_out), .sel(\控制器_regdst ));
  \寄存器堆  \u_寄存器堆  (
    .rd_rt(multiplexer_3_out), .write_enable(\控制器_regwrite ), .out_7(\寄存器堆_out_7 ), .rs(rom_1_data[11:10]),
    .out_8(\寄存器堆_out_8 ), .rt(rom_1_data[9:8]), .in_3(multiplexer_7_out), .cl(\时钟状态选择_1_out_4 ));
  assign bit_extender_1_out = {{8{rom_1_data[7]}}, rom_1_data[7:0]};  // Bit_Extender bit_extender_1
  Multiplexer #(.select(1), .width(16), .disabled("Z"), .enable("false")) multiplexer_4 (
    .in0(\寄存器堆_out_7 ), .in1(bit_extender_1_out), .out(multiplexer_4_out), .sel(\控制器_lui ));
  Multiplexer #(.select(1), .width(16), .disabled("Z"), .enable("false")) multiplexer_5 (
    .in0(\寄存器堆_out_8 ), .in1(bit_extender_1_out), .out(multiplexer_5_out), .sel(\控制器_alusrc ));
  Demultiplexer #(.select(1), .width(8), .tristate("false"), .disabled("Z"), .enable("false")) demultiplexer_1 (
    .out1(demultiplexer_1_out1), .in({4'b0000, rom_1_data[7:4]}), .sel(\控制器_display ));  // open: out0
  Demultiplexer #(.select(1), .width(8), .tristate("false"), .disabled("Z"), .enable("false")) demultiplexer_2 (
    .out1(demultiplexer_2_out1), .in({4'b0000, rom_1_data[3:0]}), .sel(\控制器_display ));  // open: out0
  ALU_test ALU (
    .out_4(ALU_out_4), .in_1(\控制器_out_13 ), .rs(multiplexer_4_out), .rt(multiplexer_6_out), .out_5(ALU_out_5));
  Multiplexer #(.select(1), .width(16), .disabled("Z"), .enable("false")) multiplexer_6 (
    .in0(multiplexer_5_out), .in1(16'h8), .out(multiplexer_6_out), .sel(\控制器_lui ));
  \_16封装加法器  \u_16封装加法器_1  (.out_3(\n16封装加法器_1_out_3 ), .in_1(\n16位移位器_1_out_3 ), .in_2(pc_1_out_3));
  \_16位移位器  \u_16位移位器_1  (.in_1(bit_extender_1_out), .out_3(\n16位移位器_1_out_3 ), .in_2(in_3));
  \bne_beq信号处理  \bne_beq信号处理_1  (.a(\控制器_unequal ), .b(ALU_out_5), .x(\bne_beq信号处理_1_x ));
  and and_1 (and_1_out, \控制器_branch , \bne_beq信号处理_1_x );
  BlockTop blocktop_1 (
    .in_1(blackbox_1_out_5), .in_2(blackbox_1_out_6), .in_3(blackbox_1_out_7), .in_4(blackbox_1_out_8),
    .out_5(blocktop_1_out_5), .out_13(blocktop_1_out_13), .out_14(blocktop_1_out_14),
    .out_6(blocktop_1_out_6), .out_7(blocktop_1_out_7), .out_15(blocktop_1_out_15),
    .out_16(blocktop_1_out_16), .out_8(blocktop_1_out_8), .out_9(blocktop_1_out_9),
    .out_17(blocktop_1_out_17), .out_18(blocktop_1_out_18), .out_10(blocktop_1_out_10),
    .out_11(blocktop_1_out_11), .out_19(blocktop_1_out_19), .out_20(blocktop_1_out_20),
    .out_12(blocktop_1_out_12));
  _7_Segment_Display #(.active("true")) u_7_segment_display_1 (
    .g(blocktop_1_out_7), .f(blocktop_1_out_15), .a(blocktop_1_out_16), .b(blocktop_1_out_8),
    .e(blockbottom_1_out_15), .d(blockbottom_1_out_7), .c(blockbottom_1_out_8), .dp(blockbottom_1_out_16));
  _7_Segment_Display #(.active("true")) u_7_segment_display_2 (
    .g(blocktop_1_out_5), .f(blocktop_1_out_13), .a(blocktop_1_out_14), .b(blocktop_1_out_6),
    .e(blockbottom_1_out_13), .d(blockbottom_1_out_5), .c(blockbottom_1_out_6), .dp(blockbottom_1_out_14));
  BlockBottom blockbottom_1 (
    .out_13(blockbottom_1_out_13), .out_5(blockbottom_1_out_5), .out_6(blockbottom_1_out_6),
    .out_14(blockbottom_1_out_14), .out_15(blockbottom_1_out_15), .out_7(blockbottom_1_out_7),
    .out_8(blockbottom_1_out_8), .out_16(blockbottom_1_out_16), .out_17(blockbottom_1_out_17),
    .out_9(blockbottom_1_out_9), .out_10(blockbottom_1_out_10), .out_18(blockbottom_1_out_18),
    .out_19(blockbottom_1_out_19), .out_11(blockbottom_1_out_11), .out_12(blockbottom_1_out_12),
    .out_20(blockbottom_1_out_20), .in_1(blackbox_1_out_5), .in_2(blackbox_1_out_6), .in_3(blackbox_1_out_7),
    .in_4(blackbox_1_out_8));
  blackbox blackbox_1 (
    .out_5(blackbox_1_out_5), .out_6(blackbox_1_out_6), .out_7(blackbox_1_out_7), .out_8(blackbox_1_out_8),
    .in_1(in_1), .in_2(in_2), .in_3(demultiplexer_1_out1), .in_4(demultiplexer_2_out1));
  not not_1 (not_1_out, \控制器_memwrite );
  _7_Segment_Display #(.active("true")) u_7_segment_display_3 (
    .g(blocktop_1_out_11), .f(blocktop_1_out_19), .a(blocktop_1_out_20), .b(blocktop_1_out_12),
    .e(blockbottom_1_out_19), .d(blockbottom_1_out_11), .c(blockbottom_1_out_12), .dp(blockbottom_1_out_20));
  _7_Segment_Display #(.active("true")) u_7_segment_display_4 (
    .g(blocktop_1_out_9), .f(blocktop_1_out_17), .a(blocktop_1_out_18), .b(blocktop_1_out_10),
    .e(blockbottom_1_out_17), .d(blockbottom_1_out_9), .c(blockbottom_1_out_10), .dp(blockbottom_1_out_18));
  RAM #(.addrWidth(16), .dataWidth(16), .bus("separate"), .Select("low")) ram_1 (
    .addr(ALU_out_4), .din(\寄存器堆_out_8 ), .data(ram_1_data), .str(\控制器_memwrite ), .clk(\时钟状态选择_1_out_3 ),
    .ld(not_1_out));  // open: sel, clr
  Multiplexer #(.select(1), .width(16), .disabled("Z"), .enable("false")) multiplexer_7 (
    .in0(ALU_out_4), .in1(ram_1_data), .out(multiplexer_7_out), .sel(\控制器_memtoreg ));

  // Notes on the sheet:
  //   自动周期
  //   pc
  //   指令寄存器
  //   contents of rom_1 (hex, n*v repeats v):
  //   2055 3044 2155 3544 91ff 796*0 100 1000 11 0 100 1000 11 0 100 1000 11 0 100 1000 11 0 100 1000 11 0
  //   100 1000 11 0 100 1000 11 0 100 1000 11 0 100 1000 11 0 100 1000 11 0 100 1000 11 0 100 1000 11 0
  //   100 1000 11 0 100 1000 11 0 100 1000 11 0 100 1000 11 0 100 1000 11 0 100 1000 11 0 100 1000 11 0
  //   100 1000 11 0 100 1000 11 0 100 1000 11 0 100 1000 11 0 100 1000 11 0 100 1000 11 0 100 1000 11 0
  //   100 1000 11 0 100 1000 11 0 100 1000 11 0 100 1000 11 0 100 1000 11 0 100 1000 11 0 100 1000 11 0
  //   100 1000 11 0 100 1000 11 0 100 1000 11 0 100 1000 11 0 100 1000 11 0 100 1000 11 0 100 1000 11 0
  //   100 1000 11 0 100 1000 11 0 100 1000 11 0 100 1000 11 0 100 1000 11 0 100 1000 11 0 100 1000 11 0
  //   100 1000 11
  //   移位器（这里看需不需要）
  //   imm
  //   jump
  //   读写
  //   rs
  //   rt
  //   rd
  //   符号扩展
  //   bne指令信号
  //   rs
  //   rt
  //   euqal信号
  //   00是or
  //   01是and
  //   10是加法
  //   11是减法（A-B）
  //   100是逻辑左移
  //   101是逻辑右移
  //   110是算数右移
  //   DISP[3]
  //   DISP[2]
  //   DISP[2]
  //   数据寄存器
  //   DISP[1]
  //   DISP[0]
  //   BlockTop
  //   BlockBottom
  //   Your Display Logic
  //   显示imm
endmodule

module control (
  input  [3:0] in_1,
  input  [2:0] in_2,
  output jump,
  output MemToReg,
  output MemWrite,
  output branch,
  output AluSrc,
  output RegWrite,
  output display,
  output regDst,
  output [1:0] out_11
);

  wire and_4_out, and_5_out, and_6_out, and_7_out, and_8_out, and_9_out, and_10_out, and_11_out, not_1_out,
       not_2_out, not_3_out, not_4_out, not_5_out, not_6_out, not_7_out, not_8_out, not_9_out, not_10_out,
       not_11_out, not_12_out, not_13_out, not_14_out, not_15_out, not_16_out, not_17_out, not_18_out,
       not_19_out, not_20_out, not_21_out, not_22_out, not_23_out, not_24_out, not_25_out, not_26_out,
       not_27_out, not_28_out;

  not not_1 (not_1_out, in_1[2]);
  not not_2 (not_2_out, in_1[1]);
  not not_3 (not_3_out, in_1[0]);
  not not_4 (not_4_out, in_1[3]);
  not not_5 (not_5_out, in_1[0]);
  not not_6 (not_6_out, in_1[3]);
  not not_7 (not_7_out, in_1[2]);
  not not_8 (not_8_out, in_1[1]);
  not not_9 (not_9_out, in_1[2]);
  not not_10 (not_10_out, in_1[0]);
  not not_11 (not_11_out, in_1[3]);
  not not_12 (not_12_out, in_1[2]);
  not not_13 (not_13_out, in_1[3]);
  not not_14 (not_14_out, in_1[1]);
  not not_15 (not_15_out, in_1[3]);
  not not_16 (not_16_out, in_1[3]);
  not not_17 (not_17_out, in_1[0]);
  not not_18 (not_18_out, in_1[3]);
  not not_19 (not_19_out, in_1[2]);
  not not_20 (not_20_out, in_1[3]);
  not not_21 (not_21_out, in_1[1]);
  not not_22 (not_22_out, in_1[3]);
  not not_23 (not_23_out, in_1[2]);
  not not_24 (not_24_out, in_1[1]);
  not not_25 (not_25_out, in_1[3]);
  not not_26 (not_26_out, in_1[2]);
  not not_27 (not_27_out, in_1[1]);
  not not_28 (not_28_out, in_1[0]);
  and and_1 (jump, in_1[3], not_1_out, not_2_out, not_3_out);
  and and_2 (MemToReg, not_4_out, in_1[2], in_1[1], not_5_out);
  and and_3 (MemWrite, not_6_out, in_1[2], in_1[1], in_1[0]);
  and and_4 (and_4_out, in_1[3], not_7_out, not_8_out, in_1[0]);
  and and_5 (and_5_out, in_1[3], not_9_out, in_1[1], not_10_out);
  and and_6 (and_6_out, not_11_out, not_12_out, in_1[1]);
  and and_7 (and_7_out, not_13_out, in_1[2], not_14_out);
  and and_8 (and_8_out, not_15_out, in_1[2], in_1[0]);
  and and_9 (and_9_out, not_16_out, not_17_out);
  and and_10 (and_10_out, not_18_out, not_19_out, in_1[1]);
  and and_11 (and_11_out, not_20_out, in_1[2], not_21_out);
  and and_12 (display, not_22_out, not_23_out, not_24_out, in_1[0]);
  and and_13 (regDst, not_25_out, not_26_out, not_27_out, not_28_out);
  or or_1 (branch, and_4_out, and_5_out);
  or or_2 (AluSrc, and_6_out, and_7_out, and_8_out);
  or or_3 (RegWrite, and_9_out, and_10_out, and_11_out);

  assign out_11 = in_2[1:0];
endmodule

module \_16封装加法器  (
  input  [15:0] in_1,
  input  [15:0] in_2,
  output [15:0] out_3
);

  \_16加法器  \u_16加法器_1  (
    .in_1(1'b0), .out_35(out_3[15]), .out_36(out_3[14]), .out_37(out_3[13]), .out_38(out_3[12]),
    .out_39(out_3[11]), .out_40(out_3[10]), .out_41(out_3[9]), .out_42(out_3[8]), .out_43(out_3[7]),
    .out_44(out_3[6]), .out_45(out_3[5]), .out_46(out_3[4]), .out_47(out_3[3]), .out_48(out_3[2]),
    .out_49(out_3[1]), .out_50(out_3[0]), .in_2(in_1[15]), .in_18(in_2[15]), .in_3(in_1[14]),
    .in_19(in_2[14]), .in_4(in_1[13]), .in_20(in_2[13]), .in_5(in_1[12]), .in_21(in_2[12]), .in_6(in_1[11]),
    .in_22(in_2[11]), .in_7(in_1[10]), .in_23(in_2[10]), .in_8(in_1[9]), .in_24(in_2[9]), .in_9(in_1[8]),
    .in_25(in_2[8]), .in_10(in_1[7]), .in_26(in_2[7]), .in_11(in_1[6]), .in_27(in_2[6]), .in_12(in_1[5]),
    .in_28(in_2[5]), .in_13(in_1[4]), .in_29(in_2[4]), .in_14(in_1[3]), .in_30(in_2[3]), .in_15(in_1[2]),
    .in_31(in_2[2]), .in_16(in_1[1]), .in_32(in_2[1]), .in_17(in_1[0]), .in_33(in_2[0]));  // open: out_51, out_34
endmodule

module temp (
  input  [3:0] in_1,
  input  [2:0] in_2,
  input  [2:0] in_3,
  output [1:0] out_4,
  output [2:0] out_5
);


  assign out_4 = in_3[1:0];
endmodule

module \_16位移位器  (
  input  [15:0] in_1,
  input  [3:0] in_2,
  output [15:0] out_3
);

  Multiplexer #(.select(4), .width(16), .disabled("Z"), .enable("false")) multiplexer_1 (
    .in0(in_1), .in1({in_1[14:0], 1'b0}), .in2({in_1[13:0], 2'b00}), .in3({in_1[12:0], 3'b000}),
    .in4({in_1[11:0], 4'b0000}), .in5({in_1[10:0], {5{1'b0}}}), .in6({in_1[9:0], {6{1'b0}}}),
    .in7({in_1[8:0], {7{1'b0}}}), .in8({in_1[7:0], {8{1'b0}}}), .in9({in_1[6:0], {9{1'b0}}}),
    .in10({in_1[5:0], {10{1'b0}}}), .in11({in_1[4:0], {11{1'b0}}}), .in12({in_1[3:0], {12{1'b0}}}),
    .in13({in_1[2:0], {13{1'b0}}}), .in14({in_1[1:0], {14{1'b0}}}), .in15({in_1[0], {15{1'b0}}}),
    .out(out_3), .sel(in_2));
endmodule

module \时钟状态选择  (
  input  in_1,
  output out_2,
  output out_3,
  output out_4
);

  wire [1:0] counter_1_q, \累加器_out_4 ;

  Demultiplexer #(.select(2), .width(1), .tristate("false"), .disabled("Z"), .enable("false")) demultiplexer_1 (
    .out0(out_2), .out1(out_3), .out2(out_4), .in(1'b1), .sel(counter_1_q));  // open: out3
  Counter #(.width(2), .max('h2), .ongoal("wrap"), .trigger("rising"), .behavior("new")) counter_1 (
    .D(\累加器_out_4 ), .Q(counter_1_q), .clk(in_1));  // open: load, count, carry, clr, preset, down
  \累加器_加1  \u_累加器  (.in_1(counter_1_q[1]), .in_2(counter_1_q[0]), .out_3(\累加器_out_4 [1]), .out_4(\累加器_out_4 [0]));
endmodule

module control_test (
  input  [3:0] in_1,
  input  [2:0] in_2,
  output jump,
  output MemToReg,
  output MemWrite,
  output branch,
  output AluSrc,
  output RegWrite,
  output display,
  output regDst,
  output lui,
  output unequal,
  output [2:0] out_13
);

  wire and_4_out, and_5_out, and_6_out, and_7_out, and_8_out, and_9_out, and_10_out, and_15_out, and_16_out,
       and_17_out, and_18_out, and_19_out, and_20_out, and_21_out, and_22_out, and_23_out, and_24_out,
       and_25_out, and_26_out, and_27_out, not_1_out, not_2_out, not_3_out, not_4_out, not_5_out, not_6_out,
       not_7_out, not_8_out, not_9_out, not_10_out, not_11_out, not_12_out, not_13_out, not_14_out,
       not_15_out, not_16_out, not_17_out, not_18_out, not_19_out, not_20_out, not_21_out, not_22_out,
       not_23_out, not_24_out, not_25_out, not_26_out, not_27_out, not_28_out, not_29_out, not_30_out,
       not_31_out, not_32_out, not_33_out, not_34_out, not_35_out, not_36_out, not_37_out, not_38_out,
       not_39_out, not_40_out, not_41_out, not_42_out, not_43_out, not_44_out, not_45_out, not_46_out,
       not_47_out, not_48_out, not_49_out, not_50_out, not_51_out;

  not not_1 (not_1_out, in_1[2]);
  not not_2 (not_2_out, in_1[1]);
  not not_3 (not_3_out, in_1[0]);
  not not_4 (not_4_out, in_1[3]);
  not not_5 (not_5_out, in_1[0]);
  not not_6 (not_6_out, in_1[3]);
  not not_7 (not_7_out, in_1[2]);
  not not_8 (not_8_out, in_1[1]);
  not not_9 (not_9_out, in_1[2]);
  not not_10 (not_10_out, in_1[0]);
  not not_11 (not_11_out, in_1[3]);
  not not_12 (not_12_out, in_1[3]);
  not not_13 (not_13_out, in_1[3]);
  not not_14 (not_14_out, in_1[0]);
  not not_15 (not_15_out, in_1[3]);
  not not_16 (not_16_out, in_1[2]);
  not not_17 (not_17_out, in_1[3]);
  not not_18 (not_18_out, in_1[1]);
  not not_19 (not_19_out, in_1[3]);
  not not_20 (not_20_out, in_1[2]);
  not not_21 (not_21_out, in_1[1]);
  not not_22 (not_22_out, in_1[3]);
  not not_23 (not_23_out, in_1[2]);
  not not_24 (not_24_out, in_1[1]);
  not not_25 (not_25_out, in_1[0]);
  not not_26 (not_26_out, in_1[3]);
  not not_27 (not_27_out, in_1[2]);
  not not_28 (not_28_out, in_1[0]);
  not not_29 (not_29_out, in_1[2]);
  not not_30 (not_30_out, in_1[0]);
  not not_31 (not_31_out, in_1[2]);
  not not_32 (not_32_out, in_1[1]);
  not not_33 (not_33_out, in_1[2]);
  not not_34 (not_34_out, in_1[0]);
  not not_35 (not_35_out, in_1[2]);
  not not_36 (not_36_out, in_1[1]);
  not not_37 (not_37_out, in_1[2]);
  not not_38 (not_38_out, in_1[0]);
  not not_39 (not_39_out, in_1[3]);
  not not_40 (not_40_out, in_1[1]);
  not not_41 (not_41_out, in_1[0]);
  not not_42 (not_42_out, in_1[3]);
  not not_43 (not_43_out, in_2[0]);
  not not_44 (not_44_out, in_2[1]);
  not not_45 (not_45_out, in_2[2]);
  and and_1 (jump, in_1[3], not_1_out, not_2_out, not_3_out);
  and and_2 (MemToReg, not_4_out, in_1[2], in_1[1], not_5_out);
  and and_3 (MemWrite, not_6_out, in_1[2], in_1[1], in_1[0]);
  and and_4 (and_4_out, in_1[3], not_7_out, not_8_out, in_1[0]);
  and and_5 (and_5_out, in_1[3], not_9_out, in_1[1], not_10_out);
  and and_6 (and_6_out, not_11_out, in_1[1]);
  and and_7 (and_7_out, not_12_out, in_1[2]);
  and and_8 (and_8_out, not_13_out, not_14_out);
  and and_9 (and_9_out, not_15_out, not_16_out, in_1[1]);
  and and_10 (and_10_out, not_17_out, in_1[2], not_18_out);
  and and_11 (display, not_19_out, not_20_out, not_21_out, in_1[0]);
  and and_12 (regDst, not_22_out, not_23_out, not_24_out, not_25_out);
  and and_13 (lui, not_26_out, not_27_out, in_1[1], not_28_out);
  and and_14 (unequal, in_1[3], not_29_out, in_1[1], not_30_out);
  and and_15 (and_15_out, not_31_out, not_32_out, in_2[0]);
  and and_16 (and_16_out, not_33_out, not_34_out, in_2[0]);
  and and_17 (and_17_out, in_1[3], in_2[0]);
  and and_18 (and_18_out, not_35_out, not_36_out, in_2[1]);
  and and_19 (and_19_out, not_37_out, not_38_out, in_2[1]);
  and and_20 (and_20_out, not_39_out, in_1[2], not_40_out, not_41_out);
  and and_21 (and_21_out, in_1[3], in_2[1]);
  not not_46 (not_46_out, in_1[2]);
  and and_22 (and_22_out, not_46_out, not_47_out, in_2[2]);
  not not_47 (not_47_out, in_1[1]);
  not not_48 (not_48_out, in_1[2]);
  not not_49 (not_49_out, in_1[0]);
  and and_23 (and_23_out, not_48_out, not_49_out, in_2[2]);
  and and_24 (and_24_out, not_42_out, in_1[1], in_1[0], not_43_out, not_44_out, not_45_out);
  not not_50 (not_50_out, in_1[3]);
  and and_25 (and_25_out, not_50_out, in_1[2], in_1[0]);
  not not_51 (not_51_out, in_1[3]);
  and and_26 (and_26_out, not_51_out, in_1[2], in_1[1]);
  and and_27 (and_27_out, in_1[3], in_2[2]);
  or or_1 (branch, and_4_out, and_5_out);
  or or_2 (AluSrc, and_6_out, and_7_out);
  or or_3 (RegWrite, and_8_out, and_9_out, and_10_out);
  or or_4 (out_13[0], and_15_out, and_16_out, and_17_out);
  or or_5 (out_13[1], and_18_out, and_19_out, and_20_out, and_21_out);
  or or_6 (out_13[2], and_22_out, and_23_out, and_24_out, and_25_out, and_26_out, and_27_out);
endmodule

module ALU_test (
  input  [2:0] in_1,
  input  [15:0] rs,
  input  [15:0] rt,
  output [15:0] out_4,
  output out_5
);

  wire not_1_out, not_2_out, not_3_out, not_4_out, not_5_out, not_6_out, not_7_out, not_8_out, not_9_out,
       not_10_out, not_11_out, not_12_out, not_13_out, not_14_out, not_15_out, not_16_out;
  wire [0:0] \减法_2_out_35 ;
  wire [15:0] and_2_out_48, or_out_48, shifter_1_out, shifter_2_out, shifter_3_out, \减法_out_50 , \加法_out_50 ;

  Multiplexer #(.select(3), .width(16), .disabled("Z"), .enable("false")) multiplexer_1 (
    .in0(or_out_48), .in1(and_2_out_48), .in2(\加法_out_50 ), .in3(\减法_out_50 ), .in4(shifter_1_out),
    .in5(shifter_2_out), .in6(shifter_3_out), .in7({{15{1'b0}}, \减法_2_out_35 [0]}), .out(out_4), .sel(in_1));
  not not_1 (not_1_out, \减法_out_50 [15]);
  and and_1 (out_5, not_1_out, not_7_out, not_3_out, not_5_out, not_2_out, not_4_out, not_8_out, not_6_out, not_10_out, not_11_out, not_15_out, not_16_out, not_12_out, not_14_out, not_13_out, not_9_out);
  not not_2 (not_2_out, \减法_out_50 [11]);
  not not_3 (not_3_out, \减法_out_50 [13]);
  not not_4 (not_4_out, \减法_out_50 [10]);
  not not_5 (not_5_out, \减法_out_50 [12]);
  not not_6 (not_6_out, \减法_out_50 [8]);
  not not_7 (not_7_out, \减法_out_50 [14]);
  not not_8 (not_8_out, \减法_out_50 [9]);
  not not_9 (not_9_out, \减法_out_50 [7]);
  or_ALU \or  (
    .out_33(or_out_48[15]), .out_34(or_out_48[14]), .out_35(or_out_48[13]), .out_36(or_out_48[12]),
    .out_37(or_out_48[11]), .out_38(or_out_48[10]), .out_39(or_out_48[9]), .out_40(or_out_48[8]),
    .out_41(or_out_48[7]), .out_42(or_out_48[6]), .out_43(or_out_48[5]), .out_44(or_out_48[4]),
    .out_45(or_out_48[3]), .out_46(or_out_48[2]), .out_47(or_out_48[1]), .out_48(or_out_48[0]),
    .in_1(rs[15]), .in_17(rt[15]), .in_2(rs[14]), .in_18(rt[14]), .in_3(rs[13]), .in_19(rt[13]),
    .in_4(rs[12]), .in_20(rt[12]), .in_5(rs[11]), .in_21(rt[11]), .in_6(rs[10]), .in_22(rt[10]),
    .in_7(rs[9]), .in_23(rt[9]), .in_8(rs[8]), .in_24(rt[8]), .in_9(rs[7]), .in_25(rt[7]), .in_10(rs[6]),
    .in_26(rt[6]), .in_11(rs[5]), .in_27(rt[5]), .in_12(rs[4]), .in_28(rt[4]), .in_13(rs[3]), .in_29(rt[3]),
    .in_14(rs[2]), .in_30(rt[2]), .in_15(rs[1]), .in_31(rt[1]), .in_16(rs[0]), .in_32(rt[0]));
  not not_10 (not_10_out, \减法_out_50 [6]);
  not not_11 (not_11_out, \减法_out_50 [5]);
  not not_12 (not_12_out, \减法_out_50 [2]);
  not not_13 (not_13_out, \减法_out_50 [0]);
  not not_14 (not_14_out, \减法_out_50 [1]);
  not not_15 (not_15_out, \减法_out_50 [4]);
  not not_16 (not_16_out, \减法_out_50 [3]);
  and_ALU and_2 (
    .out_33(and_2_out_48[15]), .out_34(and_2_out_48[14]), .out_35(and_2_out_48[13]),
    .out_36(and_2_out_48[12]), .out_37(and_2_out_48[11]), .out_38(and_2_out_48[10]),
    .out_39(and_2_out_48[9]), .out_40(and_2_out_48[8]), .out_41(and_2_out_48[7]), .out_42(and_2_out_48[6]),
    .out_43(and_2_out_48[5]), .out_44(and_2_out_48[4]), .out_45(and_2_out_48[3]), .out_46(and_2_out_48[2]),
    .out_47(and_2_out_48[1]), .out_48(and_2_out_48[0]), .in_1(rs[15]), .in_17(rt[15]), .in_2(rs[14]),
    .in_18(rt[14]), .in_3(rs[13]), .in_19(rt[13]), .in_4(rs[12]), .in_20(rt[12]), .in_5(rs[11]),
    .in_21(rt[11]), .in_6(rs[10]), .in_22(rt[10]), .in_7(rs[9]), .in_23(rt[9]), .in_8(rs[8]), .in_24(rt[8]),
    .in_9(rs[7]), .in_25(rt[7]), .in_10(rs[6]), .in_26(rt[6]), .in_11(rs[5]), .in_27(rt[5]), .in_12(rs[4]),
    .in_28(rt[4]), .in_13(rs[3]), .in_29(rt[3]), .in_14(rs[2]), .in_30(rt[2]), .in_15(rs[1]), .in_31(rt[1]),
    .in_16(rs[0]), .in_32(rt[0]));
  \_16加法器  \u_减法  (
    .in_1(1'b1), .out_35(\减法_out_50 [15]), .out_36(\减法_out_50 [14]), .out_37(\减法_out_50 [13]),
    .out_38(\减法_out_50 [12]), .out_39(\减法_out_50 [11]), .out_40(\减法_out_50 [10]), .out_41(\减法_out_50 [9]),
    .out_42(\减法_out_50 [8]), .out_43(\减法_out_50 [7]), .out_44(\减法_out_50 [6]), .out_45(\减法_out_50 [5]),
    .out_46(\减法_out_50 [4]), .out_47(\减法_out_50 [3]), .out_48(\减法_out_50 [2]), .out_49(\减法_out_50 [1]),
    .out_50(\减法_out_50 [0]), .in_2(rs[15]), .in_18(rt[15]), .in_3(rs[14]), .in_19(rt[14]), .in_4(rs[13]),
    .in_20(rt[13]), .in_5(rs[12]), .in_21(rt[12]), .in_6(rs[11]), .in_22(rt[11]), .in_7(rs[10]),
    .in_23(rt[10]), .in_8(rs[9]), .in_24(rt[9]), .in_9(rs[8]), .in_25(rt[8]), .in_10(rs[7]), .in_26(rt[7]),
    .in_11(rs[6]), .in_27(rt[6]), .in_12(rs[5]), .in_28(rt[5]), .in_13(rs[4]), .in_29(rt[4]), .in_14(rs[3]),
    .in_30(rt[3]), .in_15(rs[2]), .in_31(rt[2]), .in_16(rs[1]), .in_32(rt[1]), .in_17(rs[0]), .in_33(rt[0]));  // open: out_51, out_34
  \_16加法器  \u_加法  (
    .in_1(1'b0), .out_35(\加法_out_50 [15]), .out_36(\加法_out_50 [14]), .out_37(\加法_out_50 [13]),
    .out_38(\加法_out_50 [12]), .out_39(\加法_out_50 [11]), .out_40(\加法_out_50 [10]), .out_41(\加法_out_50 [9]),
    .out_42(\加法_out_50 [8]), .out_43(\加法_out_50 [7]), .out_44(\加法_out_50 [6]), .out_45(\加法_out_50 [5]),
    .out_46(\加法_out_50 [4]), .out_47(\加法_out_50 [3]), .out_48(\加法_out_50 [2]), .out_49(\加法_out_50 [1]),
    .out_50(\加法_out_50 [0]), .in_2(rs[15]), .in_18(rt[15]), .in_3(rs[14]), .in_19(rt[14]), .in_4(rs[13]),
    .in_20(rt[13]), .in_5(rs[12]), .in_21(rt[12]), .in_6(rs[11]), .in_22(rt[11]), .in_7(rs[10]),
    .in_23(rt[10]), .in_8(rs[9]), .in_24(rt[9]), .in_9(rs[8]), .in_25(rt[8]), .in_10(rs[7]), .in_26(rt[7]),
    .in_11(rs[6]), .in_27(rt[6]), .in_12(rs[5]), .in_28(rt[5]), .in_13(rs[4]), .in_29(rt[4]), .in_14(rs[3]),
    .in_30(rt[3]), .in_15(rs[2]), .in_31(rt[2]), .in_16(rs[1]), .in_32(rt[1]), .in_17(rs[0]), .in_33(rt[0]));  // open: out_51, out_34
  Shifter #(.width(16), .shift("ll")) shifter_1 (.in(rs), .\dist (rt[3:0]), .out(shifter_1_out));
  Shifter #(.width(16), .shift("lr")) shifter_2 (.in(rs), .\dist (rt[3:0]), .out(shifter_2_out));
  Shifter #(.width(16), .shift("ar")) shifter_3 (.in(rs), .\dist (rt[3:0]), .out(shifter_3_out));
  \_16加法器  \u_减法_2  (
    .in_1(1'b1), .out_35(\减法_2_out_35 [0]), .in_2(rs[15]), .in_18(rt[15]), .in_3(rs[14]), .in_19(rt[14]),
    .in_4(rs[13]), .in_20(rt[13]), .in_5(rs[12]), .in_21(rt[12]), .in_6(rs[11]), .in_22(rt[11]),
    .in_7(rs[10]), .in_23(rt[10]), .in_8(rs[9]), .in_24(rt[9]), .in_9(rs[8]), .in_25(rt[8]), .in_10(rs[7]),
    .in_26(rt[7]), .in_11(rs[6]), .in_27(rt[6]), .in_12(rs[5]), .in_28(rt[5]), .in_13(rs[4]), .in_29(rt[4]),
    .in_14(rs[3]), .in_30(rt[3]), .in_15(rs[2]), .in_31(rt[2]), .in_16(rs[1]), .in_32(rt[1]), .in_17(rs[0]),
    .in_33(rt[0]));  // open: out_51, out_34, out_36, out_37, out_38, out_39, out_40, out_41, out_42, out_43, out_44, out_45, out_46, out_47, out_48, out_49, out_50

  // Notes on the sheet:
  //   000是or
  //   001是and
  //   010是加法
  //   11是减法（A-B）
  //   100是逻辑左移
  //   101是逻辑右移
  //   110是算数右移
endmodule

module \bne_beq信号处理  (
  input  a,
  input  b,
  output x
);

  wire and_1_out, and_2_out, not_1_out, not_2_out;

  not not_1 (not_1_out, a);
  not not_2 (not_2_out, b);
  and and_1 (and_1_out, not_1_out, b);
  and and_2 (and_2_out, a, not_2_out);
  or or_1 (x, and_1_out, and_2_out);
endmodule

module control_test2 (
  input  [3:0] in_1,
  input  [2:0] in_2,
  output jump,
  output MemToReg,
  output MemWrite,
  output branch,
  output AluSrc,
  output RegWrite,
  output display,
  output regDst,
  output lui,
  output unequal,
  output [2:0] out_13
);

  wire and_4_out, and_5_out, and_6_out, and_7_out, and_8_out, and_9_out, and_10_out, and_15_out, and_16_out,
       and_17_out, and_18_out, and_19_out, and_20_out, and_21_out, and_22_out, and_23_out, and_24_out,
       not_1_out, not_2_out, not_3_out, not_4_out, not_5_out, not_6_out, not_7_out, not_8_out, not_9_out,
       not_10_out, not_11_out, not_12_out, not_13_out, not_14_out, not_15_out, not_16_out, not_17_out,
       not_18_out, not_19_out, not_20_out, not_21_out, not_22_out, not_23_out, not_24_out, not_25_out,
       not_26_out, not_27_out, not_28_out, not_29_out, not_30_out, not_31_out, not_32_out, not_33_out,
       not_34_out, not_35_out, not_36_out, not_37_out, not_38_out, not_39_out, not_40_out, not_41_out,
       not_42_out, not_43_out, not_44_out;

  not not_1 (not_1_out, in_1[2]);
  not not_2 (not_2_out, in_1[1]);
  not not_3 (not_3_out, in_1[0]);
  not not_4 (not_4_out, in_1[3]);
  not not_5 (not_5_out, in_1[0]);
  not not_6 (not_6_out, in_1[3]);
  not not_7 (not_7_out, in_1[2]);
  not not_8 (not_8_out, in_1[1]);
  not not_9 (not_9_out, in_1[2]);
  not not_10 (not_10_out, in_1[0]);
  not not_11 (not_11_out, in_1[3]);
  not not_12 (not_12_out, in_1[3]);
  not not_13 (not_13_out, in_1[3]);
  not not_14 (not_14_out, in_1[0]);
  not not_15 (not_15_out, in_1[3]);
  not not_16 (not_16_out, in_1[2]);
  not not_17 (not_17_out, in_1[3]);
  not not_18 (not_18_out, in_1[1]);
  not not_19 (not_19_out, in_1[3]);
  not not_20 (not_20_out, in_1[2]);
  not not_21 (not_21_out, in_1[1]);
  not not_22 (not_22_out, in_1[3]);
  not not_23 (not_23_out, in_1[2]);
  not not_24 (not_24_out, in_1[1]);
  not not_25 (not_25_out, in_1[0]);
  not not_26 (not_26_out, in_1[3]);
  not not_27 (not_27_out, in_1[2]);
  not not_28 (not_28_out, in_1[0]);
  not not_29 (not_29_out, in_1[2]);
  not not_30 (not_30_out, in_1[0]);
  not not_31 (not_31_out, in_1[2]);
  not not_32 (not_32_out, in_1[1]);
  not not_33 (not_33_out, in_1[3]);
  not not_34 (not_34_out, in_1[2]);
  not not_35 (not_35_out, in_1[0]);
  not not_36 (not_36_out, in_1[2]);
  not not_37 (not_37_out, in_1[1]);
  not not_38 (not_38_out, in_1[3]);
  not not_39 (not_39_out, in_1[0]);
  not not_40 (not_40_out, in_1[3]);
  not not_41 (not_41_out, in_1[2]);
  not not_42 (not_42_out, in_1[1]);
  not not_43 (not_43_out, in_1[3]);
  not not_44 (not_44_out, in_1[1]);
  and and_1 (jump, in_1[3], not_1_out, not_2_out, not_3_out);
  and and_2 (MemToReg, not_4_out, in_1[2], in_1[1], not_5_out);
  and and_3 (MemWrite, not_6_out, in_1[2], in_1[1], in_1[0]);
  and and_4 (and_4_out, in_1[3], not_7_out, not_8_out, in_1[0]);
  and and_5 (and_5_out, in_1[3], not_9_out, in_1[1], not_10_out);
  and and_6 (and_6_out, not_11_out, in_1[1]);
  and and_7 (and_7_out, not_12_out, in_1[2]);
  and and_8 (and_8_out, not_13_out, not_14_out);
  and and_9 (and_9_out, not_15_out, not_16_out, in_1[1]);
  and and_10 (and_10_out, not_17_out, in_1[2], not_18_out);
  and and_11 (display, not_19_out, not_20_out, not_21_out, in_1[0]);
  and and_12 (regDst, not_22_out, not_23_out, not_24_out, not_25_out);
  and and_13 (lui, not_26_out, not_27_out, in_1[1], not_28_out);
  and and_14 (unequal, in_1[3], not_29_out, in_1[1], not_30_out);
  and and_15 (and_15_out, not_31_out, not_32_out, in_2[0]);
  and and_16 (and_16_out, not_33_out, not_34_out, in_1[1], not_35_out);
  and and_17 (and_17_out, in_1[3], in_2[0]);
  and and_18 (and_18_out, not_36_out, not_37_out, in_2[1]);
  and and_19 (and_19_out, not_38_out, in_1[2], not_39_out);
  and and_20 (and_20_out, not_40_out, in_1[2], in_1[1]);
  and and_21 (and_21_out, in_1[3], in_2[1]);
  and and_22 (and_22_out, not_41_out, not_42_out, in_2[2]);
  and and_23 (and_23_out, not_43_out, in_1[2], not_44_out, in_1[0]);
  and and_24 (and_24_out, in_1[3], in_2[2]);
  or or_1 (branch, and_4_out, and_5_out);
  or or_2 (AluSrc, and_6_out, and_7_out);
  or or_3 (RegWrite, and_8_out, and_9_out, and_10_out);
  or or_4 (out_13[0], and_15_out, and_16_out, and_17_out);
  or or_5 (out_13[1], and_18_out, and_19_out, and_20_out, and_21_out);
  or or_6 (out_13[2], and_22_out, and_23_out, and_24_out);
endmodule

module \累加器_加1  (
  input  in_1,
  input  in_2,
  output out_3,
  output out_4
);

  wire fa_2_out_4, xor_1_out, xor_2_out;

  FA fa_1 (.out_5(out_3), .in_1(fa_2_out_4), .in_2(in_1), .in_3(xor_2_out));  // open: out_4
  FA fa_2 (.out_4(fa_2_out_4), .out_5(out_4), .in_1(1'b0), .in_2(in_2), .in_3(xor_1_out));
  xor xor_1 (xor_1_out, 1'b0, 1'b1);
  xor xor_2 (xor_2_out, 1'b0, 1'b0);
endmodule

module FA (
  input  in_1,
  input  in_2,
  input  in_3,
  output out_4,
  output out_5
);

  wire and_1_out, and_2_out, xor_2_out;

  or or_1 (out_4, and_1_out, and_2_out);
  and and_1 (and_1_out, in_2, in_3);
  and and_2 (and_2_out, in_1, xor_2_out);
  xor xor_1 (out_5, in_1, xor_2_out);
  xor xor_2 (xor_2_out, in_2, in_3);
endmodule
